# Fritzing sketch un_uart (saved by Fritzing 1.0.4)
circuit board: 6.09537cm x 3.62324cm
breadboards: 1

parts:
  S1 = Toggle Switch [package=THT]
  A1 = XIAO NRF52840 sense tht
  A2 = XIAO NRF52840 sense tht
  S2 = Pushbutton [package=THT]
  R1 = Resistor [tolerance=±5% power=0.25W resistance=220 package=THT]

nets:
  N1: S1.L1, A1.Pin_22
  N2: S1.COM, A2.Pin_22, R1.Pin_1
  N3: A1.Pin_2, A1.Pin_21, A2.Pin_2, A2.Pin_21, S2.leg1
  N4: A1.Pin_7, A2.Pin_7, S2.leg0, R1.Pin_0
  N5: A1.Pin_11, A2.Pin_16
  N6: A1.Pin_16, A2.Pin_11

custom parts:
  XIAO NRF52840 sense tht: The Seeed Studio XIAO family, Seeed Studio XIAO nRF52840 is equipped with a powerful Nordic nRF52840 MCU which integrates Bluetooth 5.0 connectivity. This is the THT version there is also a SMD version of the part.
